// Logisim project compuerta xor.circ as structural Verilog: 1 circuit, main circuit main
module main (
  input  in_1,
  input  [3:0] in_2,
  input  [3:0] in_3,
  output out_4,
  output [3:0] out_5
);

  wire and_1_out, and_2_out, and_3_out, and_4_out, and_5_out, and_6_out, and_7_out, and_8_out, or_1_out,
       or_2_out, or_3_out, xor_1_out, xor_2_out, xor_3_out, xor_4_out;

  xor xor_1 (xor_1_out, in_2[0], in_3[0]);
  xor xor_2 (xor_2_out, in_2[1], in_3[1]);
  xor xor_3 (xor_3_out, in_2[2], in_3[2]);
  xor xor_4 (xor_4_out, in_2[3], in_3[3]);
  and and_1 (and_1_out, in_2[0], in_3[0]);
  and and_2 (and_2_out, in_2[1], in_3[1]);
  and and_3 (and_3_out, in_2[2], in_3[2]);
  and and_4 (and_4_out, in_2[3], in_3[3]);
  and and_5 (and_5_out, xor_1_out, in_1);
  and and_6 (and_6_out, xor_2_out, or_1_out);
  and and_7 (and_7_out, xor_3_out, or_2_out);
  and and_8 (and_8_out, xor_4_out, or_3_out);
  xor xor_5 (out_5[0], xor_1_out, in_1);
  xor xor_6 (out_5[1], xor_2_out, or_1_out);
  xor xor_7 (out_5[2], xor_3_out, or_2_out);
  xor xor_8 (out_5[3], xor_4_out, or_3_out);
  or or_1 (or_1_out, and_5_out, and_1_out);
  or or_2 (or_2_out, and_6_out, and_2_out);
  or or_3 (or_3_out, and_7_out, and_3_out);
  or or_4 (out_4, and_8_out, and_4_out);
endmodule
